# Fritzing sketch optocoupler Sketch (saved by Fritzing 0.9.3b)
circuit board: 8.46667cm x 5.64444cm
breadboards: 1

parts:
  U2 = Optocoupler [package=THT]
  J1 = male pin header, 3 pins [form="♂ (male)"]
  R2 = Resistor [tolerance=±5% resistance=200 package=THT]
  R3 = Resistor [tolerance=±5% resistance=2k package=THT]
  LED1 = LED - 3mm [color="Red (633nm)" package="3 mm [THT]"]
  J2 = male pin header, 3 pins [form="♂ (male)"]
  J3 = male pin header, 1 pin [form="♂ (male)"]
  R5 = Resistor [tolerance=±5% resistance=1k package=THT]
  U3 = Optocoupler [package=THT]
  R6 = Resistor [tolerance=±5% resistance=2k package=THT]
  J4 = male pin header, 3 pins [form="♂ (male)"]
  R8 = Resistor [tolerance=±5% resistance=200 package=THT]
  J5 = male pin header, 1 pin [form="♂ (male)"]
  R9 = Resistor [tolerance=±5% resistance=1k package=THT]
  LED2 = LED - 3mm [color="Red (633nm)" package="3 mm [THT]"]

nets:
  N1: U2.Pin_1, R2.Pin_1
  N2: U2.Pin_2, J1.pin3, R3.Pin_0, U3.Pin_2, R6.Pin_0, J4.pin3
  N3: U2.Pin_4, R3.Pin_1, J2.pin3, U3.Pin_4, R6.Pin_1
  N4: U2.Pin_5, LED1.cathode
  N5: J1.pin1, R2.Pin_0
  N6: J1.pin2, J4.pin2
  N7: LED1.anode, R5.Pin_0
  N8: J3.pin1, R5.Pin_1
  N9: U3.Pin_1, R8.Pin_1
  N10: U3.Pin_5, LED2.cathode
  N11: J4.pin1, R8.Pin_0
  N12: J5.pin1, R9.Pin_1
  N13: R9.Pin_0, LED2.anode
