# Fritzing sketch Synerduino pix dash board (saved by Fritzing 0.9.3b)
circuit board: 7.8cm x 3.2359cm
breadboards: 1

parts:
  Gn_V+_0_1_2_3_4_5 = female pin header, 8 pins [form="♀ (female)"]
  LM555 = IC, DIP package, 8 pins [chip_label=IC]
  4017 = IC, DIP package, 16 pins [chip_label=IC]
  2K = Resistor [tolerance=±5% resistance=220 package=THT]
  Arm = female pin header, 2 pins [form="♀ (female)"]
  Disarm = female pin header, 2 pins [form="♀ (female)"]
  2K_2 = Resistor [tolerance=±5% resistance=220 package=THT]
  ArmLED = female pin header, 2 pins [form="♀ (female)"]
  2K_3 = Resistor [tolerance=±5% resistance=220 package=THT]
  LED1 = LED - 5mm [color="Orange (620nm)" package="5 mm [THT]"]
  Select = female pin header, 2 pins [form="♀ (female)"]
  LED2 = LED - 5mm [color="Red (633nm)" package="5 mm [THT]"]
  LED3 = LED - 5mm [color="Red (633nm)" package="5 mm [THT]"]
  LED4 = LED - 5mm [color="Blue (525nm)" package="5 mm [THT]"]
  LED5 = LED - 5mm [color="Red (633nm)" package="5 mm [THT]"]
  LED6 = LED - 5mm [color="Red (633nm)" package="5 mm [THT]"]
  LED7 = LED - 5mm [color="Red (633nm)" package="5 mm [THT]"]
  0_5K = Resistor [tolerance=±5% resistance=220 package=THT]
  0_5K_2 = Resistor [tolerance=±5% resistance=220 package=THT]
  0_5K_3 = Resistor [tolerance=±5% resistance=220 package=THT]
  0_5K_4 = Resistor [tolerance=±5% resistance=220 package=THT]
  GPSLED = female pin header, 2 pins [form="♀ (female)"]
  StatLED = female pin header, 2 pins [form="♀ (female)"]
  D45 = Rectifier Diode [part_number=1N4001 package="300 mil [THT]"]
  D13LED = female pin header, 2 pins [form="♀ (female)"]
  LED8 = LED - 5mm [color="Green (570nm)" package="5 mm [THT]"]
  C1 = Electrolytic Capacitor [capacitance=1µF package="100 mil [THT, electrolytic]"]
  2K_4 = Resistor [tolerance=±5% resistance=220 package=THT]
  2K_5 = Resistor [tolerance=±5% resistance=220 package=THT]
  Pad1 = Pad [width=2 height=2 connect=center]
  Pad2 = Pad [width=2 height=2 connect=center]
  Pad3 = Pad [width=2 height=2 connect=center]
  Pad4 = Pad [width=2 height=2 connect=center]

nets:
  N1: Gn_V+_0_1_2_3_4_5.pin1, LM555.pin1, 4017.pin8, Arm.pin1, Disarm.pin1, ArmLED.pin1, LED1.cathode, LED2.cathode, LED3.cathode, LED4.cathode, LED5.cathode, LED6.cathode, LED7.cathode, GPSLED.pin1, StatLED.pin1, D13LED.pin1, LED8.cathode, 2K_4.Pin_0, 2K_5.Pin_1
  N2: Gn_V+_0_1_2_3_4_5.pin2, LM555.pin8, 4017.pin16, 2K.Pin_0, 2K_2.Pin_0, Select.pin2, C1.+
  N3: Gn_V+_0_1_2_3_4_5.pin4, LM555.pin3, 2K_3.Pin_0
  N4: Gn_V+_0_1_2_3_4_5.pin5, 4017.pin2, 0_5K.Pin_1
  N5: Gn_V+_0_1_2_3_4_5.pin6, 4017.pin4, 0_5K_2.Pin_1
  N6: Gn_V+_0_1_2_3_4_5.pin7, 4017.pin7, 0_5K_4.Pin_0
  N7: Gn_V+_0_1_2_3_4_5.pin8, 4017.pin10, 0_5K_3.Pin_1
  N8: LM555.pin2, 2K.Pin_1, Arm.pin2
  N9: LM555.pin4, Disarm.pin2, 2K_2.Pin_1
  N10: 4017.pin1, 4017.pin15
  N11: 4017.pin11, Pad4.pad
  N12: 4017.pin12, Pad3.pad
  N13: 4017.pin13, Pad2.pad
  N14: 4017.pin14, Select.pin1, C1.-, 2K_4.Pin_1, 2K_5.Pin_0, Pad1.pad
  N15: ArmLED.pin2, LED4.anode, D45.cathode
  N16: 2K_3.Pin_1, D45.anode
  N17: LED1.anode, GPSLED.pin2
  N18: LED2.anode, 0_5K.Pin_0
  N19: LED3.anode, 0_5K_2.Pin_0
  N20: LED5.anode, 0_5K_4.Pin_1
  N21: LED6.anode, 0_5K_3.Pin_0
  N22: LED7.anode, StatLED.pin2
  N23: D13LED.pin2, LED8.anode

notes:
  B1
  PX43-V1
  PX42-V1
  SynerFlight.com
  PX42-V1.1 Addressing Dash
