# Fritzing sketch synerduino micro (saved by Fritzing 0.9.3b)
circuit board: 8cm x 2.6cm
breadboards: 1

parts:
  Synerduino_Micro_Stick_Shield = Arduino Nano (Rev3.0)
  IMU = InvenSense MPU6050
  J1 = Screw terminal - 2 pins [package=THT]
  D3 = male pin header, 3 pins [form="♂ (male)"]
  D9 = male pin header, 3 pins [form="♂ (male)"]
  D10 = male pin header, 3 pins [form="♂ (male)"]
  D11 = male pin header, 3 pins [form="♂ (male)"]
  S1 = female pin header, 4 pins [form="♀ (female)"]
  D2 = male pin header, 3 pins [form="♂ (male)"]
  G = Pad [width=1.2 height=3 connect=center]  # not connected
  3 = Pad [width=1.2 height=3 connect=center]  # not connected
  C = Pad [width=1.2 height=3 connect=center]  # not connected
  D = Pad [width=1.2 height=3 connect=center]  # not connected
  XD = Pad [width=1.2 height=3 connect=center]  # not connected
  XC = Pad [width=1.2 height=3 connect=center]  # not connected
  A = Pad [width=1.2 height=3 connect=center]  # not connected
  IN = Pad [width=1.2 height=3 connect=center]  # not connected
  J2 = rounded female pin header, 15 pins [form="♀ (female rounded)"]  # not connected
  J3 = female pin header, 15 pins [form="♀ (female)"]  # not connected

nets:
  N1: Synerduino_Micro_Stick_Shield.D1/TX, S1.pin1
  N2: Synerduino_Micro_Stick_Shield.D0/RX, S1.pin2
  N3: Synerduino_Micro_Stick_Shield.D2, D2.pin1
  N4: Synerduino_Micro_Stick_Shield.D3, D3.pin1
  N5: Synerduino_Micro_Stick_Shield.D9, D9.pin1
  N6: Synerduino_Micro_Stick_Shield.D10, D10.pin1
  N7: Synerduino_Micro_Stick_Shield.D11/MOSI, D11.pin1
  N8: Synerduino_Micro_Stick_Shield.VIN, J1.pin1, D3.pin2, D9.pin2, D10.pin2, D11.pin2, S1.pin4, D2.pin2
  N9: Synerduino_Micro_Stick_Shield.A5, IMU.SCL
  N10: Synerduino_Micro_Stick_Shield.A4, IMU.SDA
  3V3: Synerduino_Micro_Stick_Shield.3V3, IMU.VCC
  N11: IMU.GND, J1.pin2, D3.pin3, D9.pin3, D10.pin3, D11.pin3, S1.pin3, D2.pin3
