# Fritzing sketch synerduino pix (saved by Fritzing 0.9.3b)
circuit board: 5.78556cm x 20cm
circuit board: 5.78556cm x 20cm
circuit board: 13.6cm x 6.2cm
breadboards: 1

parts:
  Synerduino_PIX_Shield_V1_1 = Arduino Mega ADK (Rev3)
  J17 = male pin header, 10 pins [form="♂ (male)"]  # not connected
  J18 = double row male pin header, 36 pins [form="♂ (male)"]  # not connected
  J12 = male pin header, 8 pins [form="♂ (male)"]  # not connected
  J13 = male pin header, 8 pins [form="♂ (male)"]  # not connected
  J15 = male pin header, 8 pins [form="♂ (male)"]  # not connected
  J16 = male pin header, 8 pins [form="♂ (male)"]  # not connected
  J14 = male pin header, 8 pins [form="♂ (male)"]  # not connected
  J19 = male pin header, 16 pins [form="♂ (male)"]
  JP1 = Header 2 [package=jst-2-pth]  # not connected
  U2 = Hirose DF13 Series Header [part_number=DF13#-6P-1.25V package=DF13C-6P-1.25V]  # not connected
  Sbus = male pin header, 3 pins [form="♂ (male)"]  # not connected
  PPM = male pin header, 3 pins [form="♂ (male)"]
  J29 = male pin header, 3 pins [form="♂ (male)"]
  J30 = male pin header, 3 pins [form="♂ (male)"]
  J31 = male pin header, 3 pins [form="♂ (male)"]
  J32 = male pin header, 3 pins [form="♂ (male)"]
  J33 = male pin header, 3 pins [form="♂ (male)"]
  J34 = male pin header, 3 pins [form="♂ (male)"]
  J35 = male pin header, 3 pins [form="♂ (male)"]
  J36 = male pin header, 3 pins [form="♂ (male)"]
  D = male pin header, 8 pins [form="♂ (male)"]
  P1 = Pad [width=2 height=1.5 connect=center]
  P2 = Pad [width=2 height=1.5 connect=center]
  P3 = Pad [width=2 height=1.5 connect=center]
  P4 = Pad [width=2 height=1.5 connect=center]
  P5 = Pad [width=2 height=1.5 connect=center]
  P6 = Pad [width=2 height=1.5 connect=center]
  P7 = Pad [width=2 height=1.5 connect=center]
  P8 = Pad [width=2 height=1.5 connect=center]
  P9 = Pad [width=2 height=1.5 connect=center]
  P10 = Pad [width=2 height=1.5 connect=center]
  P11 = Pad [width=2 height=1.5 connect=center]
  P12 = Pad [width=2 height=1.5 connect=center]
  P13 = Pad [width=2 height=1.5 connect=center]
  P14 = Pad [width=2 height=1.5 connect=center]
  P15 = Pad [width=2 height=1.5 connect=center]
  P16 = Pad [width=2 height=1.5 connect=center]
  P17 = Pad [width=2 height=1.5 connect=center]  # not connected
  P18 = Pad [width=2 height=1.5 connect=center]  # not connected
  P19 = Pad [width=2 height=1.5 connect=center]
  P20 = Pad [width=2 height=1.5 connect=center]
  P21 = Pad [width=2 height=1.5 connect=center]
  P22 = Pad [width=2 height=1.5 connect=center]
  P23 = Pad [width=2 height=1.5 connect=center]
  P24 = Pad [width=2 height=1.5 connect=center]

nets:
  N1: Synerduino_PIX_Shield_V1_1.A0, P8.pad
  N2: Synerduino_PIX_Shield_V1_1.A1, P7.pad
  N3: Synerduino_PIX_Shield_V1_1.A2, P6.pad
  N4: Synerduino_PIX_Shield_V1_1.A3, P5.pad
  N5: Synerduino_PIX_Shield_V1_1.A4, P4.pad
  N6: Synerduino_PIX_Shield_V1_1.A5, P3.pad
  N7: Synerduino_PIX_Shield_V1_1.A6, P2.pad
  N8: Synerduino_PIX_Shield_V1_1.A7, P1.pad
  N9: Synerduino_PIX_Shield_V1_1.GND, J29.pin3, J30.pin3, J31.pin3, J32.pin3, J33.pin3, J34.pin3, J35.pin3, J36.pin3
  N10: Synerduino_PIX_Shield_V1_1.IOREF, Synerduino_PIX_Shield_V1_1.5V, J29.pin2, J30.pin2, J31.pin2, J32.pin2, J33.pin2, J34.pin2, J35.pin2, J36.pin2
  N11: J19.pin1, PPM.pin3
  N12: J29.pin1, P9.pad
  N13: J30.pin1, P10.pad
  N14: J31.pin1, P11.pad
  N15: J32.pin1, P12.pad
  N16: J33.pin1, P13.pad
  N17: J34.pin1, P14.pad
  N18: J35.pin1, P15.pad
  N19: J36.pin1, P16.pad
  N20: D.pin1, P24.pad
  N21: D.pin2, P23.pad
  N22: D.pin3, P22.pad
  N23: D.pin4, P21.pad
  N24: D.pin5, P20.pad
  N25: D.pin6, P19.pad

notes:
  www.synerflight.com
  ~ + -
  Telemetey
