# Fritzing sketch synerduino pix2-analog (saved by Fritzing 0.9.3b)
circuit board: 5.78556cm x 20cm
circuit board: 13.6cm x 6.2cm
circuit board: 5.78556cm x 20cm
circuit board: 13.6cm x 6.2cm
breadboards: 1

parts:
  J17 = male pin header, 10 pins [form="♂ (male)"]  # not connected
  J18 = double row male pin header, 36 pins [form="♂ (male)"]  # not connected
  J12 = male pin header, 8 pins [form="♂ (male)"]  # not connected
  J13 = male pin header, 8 pins [form="♂ (male)"]  # not connected
  J15 = male pin header, 8 pins [form="♂ (male)"]  # not connected
  J16 = male pin header, 8 pins [form="♂ (male)"]  # not connected
  J14 = male pin header, 8 pins [form="♂ (male)"]  # not connected
  J1 = male pin header, 16 pins [form="♂ (male)"]
  CH8 = male pin header, 3 pins [form="♂ (male)"]
  CH7 = male pin header, 3 pins [form="♂ (male)"]
  CH6 = male pin header, 3 pins [form="♂ (male)"]
  CH5 = male pin header, 3 pins [form="♂ (male)"]
  CH5_2 = male pin header, 3 pins [form="♂ (male)"]
  CH3 = male pin header, 3 pins [form="♂ (male)"]
  CH2 = male pin header, 3 pins [form="♂ (male)"]
  CH1 = male pin header, 3 pins [form="♂ (male)"]
  A7 = Pad [width=2 height=1.5 connect=center]
  A6 = Pad [width=2 height=1.5 connect=center]
  A5 = Pad [width=2 height=1.5 connect=center]
  A4 = Pad [width=2 height=1.5 connect=center]
  A3 = Pad [width=2 height=1.5 connect=center]
  A2 = Pad [width=2 height=1.5 connect=center]
  A1 = Pad [width=2 height=1.5 connect=center]
  A0 = Pad [width=2 height=1.5 connect=center]
  P8 = Pad [width=2 height=1.5 connect=center]
  P7 = Pad [width=2 height=1.5 connect=center]
  P6 = Pad [width=2 height=1.5 connect=center]
  P5 = Pad [width=2 height=1.5 connect=center]
  P4 = Pad [width=2 height=1.5 connect=center]
  P3 = Pad [width=2 height=1.5 connect=center]
  P2 = Pad [width=2 height=1.5 connect=center]
  P1 = Pad [width=2 height=1.5 connect=center]
  D9 = Pad [width=2 height=1.5 connect=center]
  D8 = Pad [width=2 height=1.5 connect=center]
  D7 = Pad [width=2 height=1.5 connect=center]
  D6 = Pad [width=2 height=1.5 connect=center]
  D5 = Pad [width=2 height=1.5 connect=center]
  D4 = Pad [width=2 height=1.5 connect=center]
  D3 = Pad [width=2 height=1.5 connect=center]
  D2 = Pad [width=2 height=1.5 connect=center]
  J2 = male pin header, 16 pins [form="♂ (male)"]
  J3 = male pin header, 16 pins [form="♂ (male)"]
  J4 = female pin header, 8 pins [form="♀ (female)"]
  PPM = female pin header, 3 pins [form="♀ (female)"]
  Sbus = female pin header, 3 pins [form="♀ (female)"]
  J5 = male pin header, 10 pins [form="♂ (male)"]
  J6 = male pin header, 8 pins [form="♂ (male)"]
  J7 = female pin header, 4 pins [form="♀ (female)"]
  J9 = female pin header, 4 pins [form="♀ (female)"]
  J10 = female pin header, 4 pins [form="♀ (female)"]
  J12_2 = female pin header, 4 pins [form="♀ (female)"]
  J6_2 = male pin header, 10 pins [form="♂ (male)"]
  J8 = male pin header, 4 pins [form="♂ (male)"]
  J11 = male pin header, 4 pins [form="♂ (male)"]
  switch1 = Rotary_Switch_12x1
  ACH1 = male pin header, 3 pins [form="♂ (male)"]
  ACH2 = male pin header, 3 pins [form="♂ (male)"]
  ACH3 = male pin header, 3 pins [form="♂ (male)"]
  ACH4 = male pin header, 3 pins [form="♂ (male)"]
  BCH1 = male pin header, 3 pins [form="♂ (male)"]
  BCH2 = male pin header, 3 pins [form="♂ (male)"]
  BCH3 = male pin header, 3 pins [form="♂ (male)"]
  BCH4 = male pin header, 3 pins [form="♂ (male)"]
  CCH1 = male pin header, 3 pins [form="♂ (male)"]
  CCH2 = male pin header, 3 pins [form="♂ (male)"]
  CCH3 = male pin header, 3 pins [form="♂ (male)"]
  CCH4 = male pin header, 3 pins [form="♂ (male)"]
  Synerduino_AGAV_Companion_Shield_V1_1 = Arduino Mega ADK (Rev3)
  switch2 = Rotary_Switch_12x1
  ACH5 = male pin header, 3 pins [form="♂ (male)"]
  ACH6 = male pin header, 3 pins [form="♂ (male)"]
  ACH7 = male pin header, 3 pins [form="♂ (male)"]
  BCH5 = male pin header, 3 pins [form="♂ (male)"]
  CCH5 = male pin header, 3 pins [form="♂ (male)"]
  CCH6 = male pin header, 3 pins [form="♂ (male)"]
  ACH8 = male pin header, 3 pins [form="♂ (male)"]
  CCH7 = male pin header, 3 pins [form="♂ (male)"]
  BCH6 = male pin header, 3 pins [form="♂ (male)"]
  BCH7 = male pin header, 3 pins [form="♂ (male)"]
  CCH8 = male pin header, 3 pins [form="♂ (male)"]
  BCH8 = male pin header, 3 pins [form="♂ (male)"]

nets:
  N1: J1.pin1, PPM.pin3
  N2: J1.pin2, Sbus.pin1
  N3: J1.pin7, switch1.0
  N4: CH8.pin1, P8.pad
  N5: CH8.pin2, CH7.pin2, CH6.pin2, CH5.pin2, CH5_2.pin2, CH3.pin2, CH2.pin2, CH1.pin2, J2.pin1, J2.pin2, J2.pin3, J2.pin4, J2.pin5, J2.pin6, J2.pin7, J2.pin8, J2.pin9, J2.pin10, J2.pin11, J2.pin12, J2.pin13, J2.pin14, J2.pin15, J2.pin16, PPM.pin2, J5.pin9, J6.pin7, Synerduino_AGAV_Companion_Shield_V1_1.VIN
  N6: CH8.pin3, CH7.pin3, CH6.pin3, CH5.pin3, CH5_2.pin3, CH3.pin3, CH2.pin3, CH1.pin3, J3.pin1, J3.pin2, J3.pin3, J3.pin4, J3.pin5, J3.pin6, J3.pin7, J3.pin8, J3.pin9, J3.pin10, J3.pin11, J3.pin12, J3.pin13, J3.pin14, J3.pin15, J3.pin16, PPM.pin1, Sbus.pin3, J5.pin10, J6.pin8, J12_2.pin1, J6_2.pin1, J11.pin4, Synerduino_AGAV_Companion_Shield_V1_1.GND
  N7: CH7.pin1, P7.pad
  N8: CH6.pin1, P6.pad
  N9: CH5.pin1, P5.pad
  N10: CH5_2.pin1, P4.pad
  N11: CH3.pin1, P3.pad
  N12: CH2.pin1, P2.pad
  N13: CH1.pin1, P1.pad
  N14: A7.pad, Synerduino_AGAV_Companion_Shield_V1_1.A7
  N15: A6.pad, Synerduino_AGAV_Companion_Shield_V1_1.A6
  N16: A5.pad, Synerduino_AGAV_Companion_Shield_V1_1.A5
  N17: A4.pad, Synerduino_AGAV_Companion_Shield_V1_1.A4
  N18: A3.pad, Synerduino_AGAV_Companion_Shield_V1_1.A3
  N19: A2.pad, Synerduino_AGAV_Companion_Shield_V1_1.A2
  N20: A1.pad, Synerduino_AGAV_Companion_Shield_V1_1.A1
  N21: A0.pad, Synerduino_AGAV_Companion_Shield_V1_1.A0
  N22: D9.pad, J4.pin8, J5.pin1, J6.pin2, Synerduino_AGAV_Companion_Shield_V1_1.D9_PWM
  N23: D8.pad, J4.pin7, J5.pin2, J6.pin1, Synerduino_AGAV_Companion_Shield_V1_1.D8_PWM
  N24: D7.pad, J4.pin6, J5.pin3, Synerduino_AGAV_Companion_Shield_V1_1.D7_PWM
  N25: D6.pad, J4.pin5, J5.pin4, Synerduino_AGAV_Companion_Shield_V1_1.D6_PWM
  N26: D5.pad, J4.pin4, J5.pin5, Synerduino_AGAV_Companion_Shield_V1_1.D5_PWM
  N27: D4.pad, J4.pin3, J5.pin6, Synerduino_AGAV_Companion_Shield_V1_1.D4_PWM
  N28: D3.pad, J4.pin2, J5.pin7, Synerduino_AGAV_Companion_Shield_V1_1.D3_PWM
  N29: D2.pad, J4.pin1, J5.pin8, Synerduino_AGAV_Companion_Shield_V1_1.D2_PWM
  N30: J6.pin3, Synerduino_AGAV_Companion_Shield_V1_1.D10_PWM
  N31: J6.pin4, Synerduino_AGAV_Companion_Shield_V1_1.D11_PWM
  N32: J6.pin5, Synerduino_AGAV_Companion_Shield_V1_1.D12_PWM
  N33: J6.pin6, Synerduino_AGAV_Companion_Shield_V1_1.D13_PWM
  N34: J7.pin1, J9.pin1, J10.pin1, J8.pin4
  N35: J7.pin2, Synerduino_AGAV_Companion_Shield_V1_1.D22
  N36: J7.pin3, Synerduino_AGAV_Companion_Shield_V1_1.D23
  N37: J7.pin4, J10.pin4, J6_2.pin2, J8.pin1, J11.pin1, Synerduino_AGAV_Companion_Shield_V1_1.IOREF, Synerduino_AGAV_Companion_Shield_V1_1.5V
  N38: J9.pin2, J8.pin3
  N39: J9.pin3, J8.pin2
  N40: J10.pin2, Synerduino_AGAV_Companion_Shield_V1_1.D24
  N41: J10.pin3, Synerduino_AGAV_Companion_Shield_V1_1.D25
  N42: J12_2.pin2, J11.pin3
  N43: J12_2.pin3, J11.pin2
  N44: J6_2.pin3, Synerduino_AGAV_Companion_Shield_V1_1.A15
  N45: J6_2.pin4, Synerduino_AGAV_Companion_Shield_V1_1.A14
  N46: J6_2.pin5, Synerduino_AGAV_Companion_Shield_V1_1.A13
  N47: J6_2.pin6, Synerduino_AGAV_Companion_Shield_V1_1.A12
  N48: J6_2.pin7, Synerduino_AGAV_Companion_Shield_V1_1.A11
  N49: J6_2.pin8, Synerduino_AGAV_Companion_Shield_V1_1.A10
  N50: J6_2.pin9, Synerduino_AGAV_Companion_Shield_V1_1.A9
  N51: J6_2.pin10, Synerduino_AGAV_Companion_Shield_V1_1.A8
  N52: switch1.1, CCH4.pin1
  N53: switch1.2, ACH3.pin1
  N54: switch1.3, BCH3.pin1
  N55: switch1.4, CCH3.pin1
  N56: switch1.5, ACH2.pin1
  N57: switch1.6, BCH2.pin1
  N58: switch1.7, CCH2.pin1
  N59: switch1.8, ACH1.pin1
  N60: switch1.9, BCH1.pin1
  N61: switch1.10, CCH1.pin1
  N62: switch1.11, ACH4.pin1
  N63: switch1.12, BCH4.pin1
  N64: switch2.1, CCH6.pin1
  N65: switch2.2, ACH6.pin1
  N66: switch2.3, BCH8.pin1
  N67: switch2.4, CCH7.pin1
  N68: switch2.5, ACH7.pin1
  N69: switch2.6, BCH5.pin1
  N70: switch2.7, CCH5.pin1
  N71: switch2.8, ACH5.pin1
  N72: switch2.9, BCH7.pin1
  N73: switch2.10, CCH8.pin1
  N74: switch2.11, ACH8.pin1
  N75: switch2.12, BCH6.pin1

notes:
  www.synerflight.com
  ~ + -
  Telemetey
  - + ~
  1A
  2A
  3A
  4A
  1B
  2B
  3B
  4B
  1C
  2C
  3C
  4C
