# Fritzing sketch synerduino pix2 (saved by Fritzing 0.9.3b)
circuit board: 5.78556cm x 20cm
circuit board: 5.78556cm x 20cm
circuit board: 13.6cm x 6.2cm
breadboards: 1

parts:
  Synerduino_AGAV_Companion_Shield_V1_1 = Arduino Mega ADK (Rev3)
  J17 = male pin header, 10 pins [form="♂ (male)"]  # not connected
  J18 = double row male pin header, 36 pins [form="♂ (male)"]  # not connected
  J12 = male pin header, 8 pins [form="♂ (male)"]  # not connected
  J13 = male pin header, 8 pins [form="♂ (male)"]  # not connected
  J15 = male pin header, 8 pins [form="♂ (male)"]  # not connected
  J16 = male pin header, 8 pins [form="♂ (male)"]  # not connected
  J14 = male pin header, 8 pins [form="♂ (male)"]  # not connected
  J1 = male pin header, 16 pins [form="♂ (male)"]
  CH8 = male pin header, 3 pins [form="♂ (male)"]
  CH7 = male pin header, 3 pins [form="♂ (male)"]
  CH6 = male pin header, 3 pins [form="♂ (male)"]
  CH5 = male pin header, 3 pins [form="♂ (male)"]
  CH5_2 = male pin header, 3 pins [form="♂ (male)"]
  CH3 = male pin header, 3 pins [form="♂ (male)"]
  CH2 = male pin header, 3 pins [form="♂ (male)"]
  CH1 = male pin header, 3 pins [form="♂ (male)"]
  A7 = Pad [width=2 height=1.5 connect=center]
  A6 = Pad [width=2 height=1.5 connect=center]
  A5 = Pad [width=2 height=1.5 connect=center]
  A4 = Pad [width=2 height=1.5 connect=center]
  A3 = Pad [width=2 height=1.5 connect=center]
  A2 = Pad [width=2 height=1.5 connect=center]
  A1 = Pad [width=2 height=1.5 connect=center]
  A0 = Pad [width=2 height=1.5 connect=center]
  P8 = Pad [width=2 height=1.5 connect=center]
  P7 = Pad [width=2 height=1.5 connect=center]
  P6 = Pad [width=2 height=1.5 connect=center]
  P5 = Pad [width=2 height=1.5 connect=center]
  P4 = Pad [width=2 height=1.5 connect=center]
  P3 = Pad [width=2 height=1.5 connect=center]
  P2 = Pad [width=2 height=1.5 connect=center]
  P1 = Pad [width=2 height=1.5 connect=center]
  D9 = Pad [width=2 height=1.5 connect=center]
  D8 = Pad [width=2 height=1.5 connect=center]
  D7 = Pad [width=2 height=1.5 connect=center]
  D6 = Pad [width=2 height=1.5 connect=center]
  D5 = Pad [width=2 height=1.5 connect=center]
  D4 = Pad [width=2 height=1.5 connect=center]
  D3 = Pad [width=2 height=1.5 connect=center]
  D2 = Pad [width=2 height=1.5 connect=center]
  J2 = male pin header, 16 pins [form="♂ (male)"]
  J3 = male pin header, 16 pins [form="♂ (male)"]
  J4 = female pin header, 8 pins [form="♀ (female)"]
  PPM = female pin header, 3 pins [form="♀ (female)"]
  Sbus = female pin header, 3 pins [form="♀ (female)"]
  J5 = male pin header, 10 pins [form="♂ (male)"]
  J6 = male pin header, 8 pins [form="♂ (male)"]
  J7 = female pin header, 4 pins [form="♀ (female)"]
  J9 = female pin header, 4 pins [form="♀ (female)"]
  J10 = female pin header, 4 pins [form="♀ (female)"]
  J12_2 = female pin header, 4 pins [form="♀ (female)"]
  J6_2 = male pin header, 10 pins [form="♂ (male)"]
  J8 = male pin header, 4 pins [form="♂ (male)"]
  J11 = male pin header, 4 pins [form="♂ (male)"]

nets:
  N1: Synerduino_AGAV_Companion_Shield_V1_1.A8, J6_2.pin10
  N2: Synerduino_AGAV_Companion_Shield_V1_1.A9, J6_2.pin9
  N3: Synerduino_AGAV_Companion_Shield_V1_1.A10, J6_2.pin8
  N4: Synerduino_AGAV_Companion_Shield_V1_1.A11, J6_2.pin7
  N5: Synerduino_AGAV_Companion_Shield_V1_1.A12, J6_2.pin6
  N6: Synerduino_AGAV_Companion_Shield_V1_1.A13, J6_2.pin5
  N7: Synerduino_AGAV_Companion_Shield_V1_1.A14, J6_2.pin4
  N8: Synerduino_AGAV_Companion_Shield_V1_1.A15, J6_2.pin3
  N9: Synerduino_AGAV_Companion_Shield_V1_1.A0, A0.pad
  N10: Synerduino_AGAV_Companion_Shield_V1_1.A1, A1.pad
  N11: Synerduino_AGAV_Companion_Shield_V1_1.A2, A2.pad
  N12: Synerduino_AGAV_Companion_Shield_V1_1.A3, A3.pad
  N13: Synerduino_AGAV_Companion_Shield_V1_1.A4, A4.pad
  N14: Synerduino_AGAV_Companion_Shield_V1_1.A5, A5.pad
  N15: Synerduino_AGAV_Companion_Shield_V1_1.A6, A6.pad
  N16: Synerduino_AGAV_Companion_Shield_V1_1.A7, A7.pad
  N17: Synerduino_AGAV_Companion_Shield_V1_1.GND, CH8.pin3, CH7.pin3, CH6.pin3, CH5.pin3, CH5_2.pin3, CH3.pin3, CH2.pin3, CH1.pin3, J3.pin1, J3.pin2, J3.pin3, J3.pin4, J3.pin5, J3.pin6, J3.pin7, J3.pin8, J3.pin9, J3.pin10, J3.pin11, J3.pin12, J3.pin13, J3.pin14, J3.pin15, J3.pin16, PPM.pin1, Sbus.pin3, J5.pin10, J6.pin8, J12_2.pin1, J6_2.pin1, J11.pin4
  N18: Synerduino_AGAV_Companion_Shield_V1_1.D13_PWM, J6.pin6
  N19: Synerduino_AGAV_Companion_Shield_V1_1.D12_PWM, J6.pin5
  N20: Synerduino_AGAV_Companion_Shield_V1_1.D11_PWM, J6.pin4
  N21: Synerduino_AGAV_Companion_Shield_V1_1.D10_PWM, J6.pin3
  N22: Synerduino_AGAV_Companion_Shield_V1_1.D9_PWM, D9.pad, J4.pin8, J5.pin1, J6.pin2
  N23: Synerduino_AGAV_Companion_Shield_V1_1.D8_PWM, D8.pad, J4.pin7, J5.pin2, J6.pin1
  N24: Synerduino_AGAV_Companion_Shield_V1_1.IOREF, Synerduino_AGAV_Companion_Shield_V1_1.5V, J7.pin4, J10.pin4, J6_2.pin2, J8.pin1, J11.pin1
  N25: Synerduino_AGAV_Companion_Shield_V1_1.VIN, CH8.pin2, CH7.pin2, CH6.pin2, CH5.pin2, CH5_2.pin2, CH3.pin2, CH2.pin2, CH1.pin2, J2.pin1, J2.pin2, J2.pin3, J2.pin4, J2.pin5, J2.pin6, J2.pin7, J2.pin8, J2.pin9, J2.pin10, J2.pin11, J2.pin12, J2.pin13, J2.pin14, J2.pin15, J2.pin16, PPM.pin2, J5.pin9, J6.pin7
  N26: Synerduino_AGAV_Companion_Shield_V1_1.D2_PWM, D2.pad, J4.pin1, J5.pin8
  N27: Synerduino_AGAV_Companion_Shield_V1_1.D3_PWM, D3.pad, J4.pin2, J5.pin7
  N28: Synerduino_AGAV_Companion_Shield_V1_1.D4_PWM, D4.pad, J4.pin3, J5.pin6
  N29: Synerduino_AGAV_Companion_Shield_V1_1.D5_PWM, D5.pad, J4.pin4, J5.pin5
  N30: Synerduino_AGAV_Companion_Shield_V1_1.D6_PWM, D6.pad, J4.pin5, J5.pin4
  N31: Synerduino_AGAV_Companion_Shield_V1_1.D7_PWM, D7.pad, J4.pin6, J5.pin3
  N32: Synerduino_AGAV_Companion_Shield_V1_1.D22, J7.pin2
  N33: Synerduino_AGAV_Companion_Shield_V1_1.D23, J7.pin3
  N34: Synerduino_AGAV_Companion_Shield_V1_1.D24, J10.pin2
  N35: Synerduino_AGAV_Companion_Shield_V1_1.D25, J10.pin3
  N36: J1.pin1, PPM.pin3
  N37: J1.pin2, Sbus.pin1
  N38: CH8.pin1, P8.pad
  N39: CH7.pin1, P7.pad
  N40: CH6.pin1, P6.pad
  N41: CH5.pin1, P5.pad
  N42: CH5_2.pin1, P4.pad
  N43: CH3.pin1, P3.pad
  N44: CH2.pin1, P2.pad
  N45: CH1.pin1, P1.pad
  N46: J7.pin1, J9.pin1, J10.pin1, J8.pin4
  N47: J9.pin2, J8.pin3
  N48: J9.pin3, J8.pin2
  N49: J12_2.pin2, J11.pin3
  N50: J12_2.pin3, J11.pin2

notes:
  www.synerflight.com
  ~ + -
  Telemetey
  - + ~
