# Fritzing sketch synerduino pix3-analog1 (saved by Fritzing 0.9.3b)
circuit board: 5.78556cm x 20cm
circuit board: 4.10404cm x 3.33229cm
circuit board: 5.78556cm x 20cm
circuit board: 13.6cm x 6.2cm
breadboards: 1

parts:
  J17 = male pin header, 10 pins [form="♂ (male)"]  # not connected
  J18 = double row male pin header, 36 pins [form="♂ (male)"]  # not connected
  J12 = male pin header, 8 pins [form="♂ (male)"]  # not connected
  J13 = male pin header, 8 pins [form="♂ (male)"]  # not connected
  J15 = male pin header, 8 pins [form="♂ (male)"]  # not connected
  J16 = male pin header, 8 pins [form="♂ (male)"]  # not connected
  J14 = male pin header, 8 pins [form="♂ (male)"]  # not connected
  J1 = male pin header, 16 pins [form="♂ (male)"]
  CH8 = male pin header, 3 pins [form="♂ (male)"]
  CH7 = male pin header, 3 pins [form="♂ (male)"]
  CH6 = male pin header, 3 pins [form="♂ (male)"]
  CH5 = male pin header, 3 pins [form="♂ (male)"]
  CH5_2 = male pin header, 3 pins [form="♂ (male)"]
  CH3 = male pin header, 3 pins [form="♂ (male)"]
  CH2 = male pin header, 3 pins [form="♂ (male)"]
  CH1 = male pin header, 3 pins [form="♂ (male)"]
  A7 = Pad [width=2 height=1.5 connect=center]
  A6 = Pad [width=2 height=1.5 connect=center]
  A5 = Pad [width=2 height=1.5 connect=center]
  A4 = Pad [width=2 height=1.5 connect=center]
  A3 = Pad [width=2 height=1.5 connect=center]
  A2 = Pad [width=2 height=1.5 connect=center]
  A1 = Pad [width=2 height=1.5 connect=center]
  A0 = Pad [width=2 height=1.5 connect=center]
  P8 = Pad [width=2 height=1.5 connect=center]
  P7 = Pad [width=2 height=1.5 connect=center]
  P6 = Pad [width=2 height=1.5 connect=center]
  P5 = Pad [width=2 height=1.5 connect=center]
  P4 = Pad [width=2 height=1.5 connect=center]
  P3 = Pad [width=2 height=1.5 connect=center]
  P2 = Pad [width=2 height=1.5 connect=center]
  P1 = Pad [width=2 height=1.5 connect=center]
  D9 = Pad [width=2 height=1.5 connect=center]
  D8 = Pad [width=2 height=1.5 connect=center]
  D7 = Pad [width=2 height=1.5 connect=center]
  D6 = Pad [width=2 height=1.5 connect=center]
  D5 = Pad [width=2 height=1.5 connect=center]
  D4 = Pad [width=2 height=1.5 connect=center]
  D3 = Pad [width=2 height=1.5 connect=center]
  D2 = Pad [width=2 height=1.5 connect=center]
  J2 = male pin header, 16 pins [form="♂ (male)"]
  J3 = male pin header, 16 pins [form="♂ (male)"]
  J4 = female pin header, 8 pins [form="♀ (female)"]
  PPM = female pin header, 3 pins [form="♀ (female)"]
  Sbus = female pin header, 3 pins [form="♀ (female)"]
  J5 = male pin header, 10 pins [form="♂ (male)"]
  J6 = male pin header, 8 pins [form="♂ (male)"]
  J7 = female pin header, 4 pins [form="♀ (female)"]
  J9 = female pin header, 4 pins [form="♀ (female)"]
  J10 = female pin header, 4 pins [form="♀ (female)"]
  J12_2 = female pin header, 4 pins [form="♀ (female)"]
  J6_2 = male pin header, 10 pins [form="♂ (male)"]
  J8 = male pin header, 4 pins [form="♂ (male)"]
  J11 = male pin header, 4 pins [form="♂ (male)"]
  ACH1 = male pin header, 3 pins [form="♂ (male)"]  # not connected
  ACH2 = male pin header, 3 pins [form="♂ (male)"]  # not connected
  ACH3 = male pin header, 3 pins [form="♂ (male)"]  # not connected
  ACH4 = male pin header, 3 pins [form="♂ (male)"]  # not connected
  BCH1 = male pin header, 3 pins [form="♂ (male)"]  # not connected
  BCH2 = male pin header, 3 pins [form="♂ (male)"]  # not connected
  BCH3 = male pin header, 3 pins [form="♂ (male)"]  # not connected
  CCH1 = male pin header, 3 pins [form="♂ (male)"]  # not connected
  CCH2 = male pin header, 3 pins [form="♂ (male)"]  # not connected
  Synerduino_AGAV_Companion_Shield_V1_1 = Arduino Mega ADK (Rev3)
  switch2 = Rotary_Switch_12x1
  J19 = male pin header, 12 pins [form="♂ (male)"]
  J20 = female pin header, 4 pins [form="♀ (female)"]
  CCH3 = male pin header, 3 pins [form="♂ (male)"]  # not connected
  CCH4 = male pin header, 3 pins [form="♂ (male)"]  # not connected
  J21 = male pin header, 12 pins [form="♂ (male)"]  # not connected
  J22 = female pin header, 4 pins [form="♀ (female)"]

nets:
  N1: J1.pin1, PPM.pin3
  N2: J1.pin2, Sbus.pin1
  N3: J1.pin7, J22.pin1
  N4: J1.pin8, J22.pin2
  N5: J1.pin9, J22.pin3
  N6: J1.pin10, J22.pin4
  N7: CH8.pin1, P8.pad
  N8: CH8.pin2, CH7.pin2, CH6.pin2, CH5.pin2, CH5_2.pin2, CH3.pin2, CH2.pin2, CH1.pin2, J2.pin1, J2.pin2, J2.pin3, J2.pin4, J2.pin5, J2.pin6, J2.pin7, J2.pin8, J2.pin9, J2.pin10, J2.pin11, J2.pin12, J2.pin13, J2.pin14, J2.pin15, J2.pin16, PPM.pin2, J5.pin9, J6.pin7, Synerduino_AGAV_Companion_Shield_V1_1.VIN
  N9: CH8.pin3, CH7.pin3, CH6.pin3, CH5.pin3, CH5_2.pin3, CH3.pin3, CH2.pin3, CH1.pin3, J3.pin1, J3.pin2, J3.pin3, J3.pin4, J3.pin5, J3.pin6, J3.pin7, J3.pin8, J3.pin9, J3.pin10, J3.pin11, J3.pin12, J3.pin13, J3.pin14, J3.pin15, J3.pin16, PPM.pin1, Sbus.pin3, J5.pin10, J6.pin8, J12_2.pin1, J6_2.pin1, J11.pin4, Synerduino_AGAV_Companion_Shield_V1_1.GND
  N10: CH7.pin1, P7.pad
  N11: CH6.pin1, P6.pad
  N12: CH5.pin1, P5.pad
  N13: CH5_2.pin1, P4.pad
  N14: CH3.pin1, P3.pad
  N15: CH2.pin1, P2.pad
  N16: CH1.pin1, P1.pad
  N17: A7.pad, Synerduino_AGAV_Companion_Shield_V1_1.A7
  N18: A6.pad, Synerduino_AGAV_Companion_Shield_V1_1.A6
  N19: A5.pad, Synerduino_AGAV_Companion_Shield_V1_1.A5
  N20: A4.pad, Synerduino_AGAV_Companion_Shield_V1_1.A4
  N21: A3.pad, Synerduino_AGAV_Companion_Shield_V1_1.A3
  N22: A2.pad, Synerduino_AGAV_Companion_Shield_V1_1.A2
  N23: A1.pad, Synerduino_AGAV_Companion_Shield_V1_1.A1
  N24: A0.pad, Synerduino_AGAV_Companion_Shield_V1_1.A0
  N25: D9.pad, J4.pin8, J5.pin1, J6.pin2, Synerduino_AGAV_Companion_Shield_V1_1.D9_PWM
  N26: D8.pad, J4.pin7, J5.pin2, J6.pin1, Synerduino_AGAV_Companion_Shield_V1_1.D8_PWM
  N27: D7.pad, J4.pin6, J5.pin3, Synerduino_AGAV_Companion_Shield_V1_1.D7_PWM
  N28: D6.pad, J4.pin5, J5.pin4, Synerduino_AGAV_Companion_Shield_V1_1.D6_PWM
  N29: D5.pad, J4.pin4, J5.pin5, Synerduino_AGAV_Companion_Shield_V1_1.D5_PWM
  N30: D4.pad, J4.pin3, J5.pin6, Synerduino_AGAV_Companion_Shield_V1_1.D4_PWM
  N31: D3.pad, J4.pin2, J5.pin7, Synerduino_AGAV_Companion_Shield_V1_1.D3_PWM
  N32: D2.pad, J4.pin1, J5.pin8, Synerduino_AGAV_Companion_Shield_V1_1.D2_PWM
  N33: J6.pin3, Synerduino_AGAV_Companion_Shield_V1_1.D10_PWM
  N34: J6.pin4, Synerduino_AGAV_Companion_Shield_V1_1.D11_PWM
  N35: J6.pin5, Synerduino_AGAV_Companion_Shield_V1_1.D12_PWM
  N36: J6.pin6, Synerduino_AGAV_Companion_Shield_V1_1.D13_PWM
  N37: J7.pin1, J9.pin1, J10.pin1, J8.pin4
  N38: J7.pin2, Synerduino_AGAV_Companion_Shield_V1_1.D22
  N39: J7.pin3, Synerduino_AGAV_Companion_Shield_V1_1.D23
  N40: J7.pin4, J10.pin4, J6_2.pin2, J8.pin1, J11.pin1, Synerduino_AGAV_Companion_Shield_V1_1.IOREF, Synerduino_AGAV_Companion_Shield_V1_1.5V
  N41: J9.pin2, J8.pin3
  N42: J9.pin3, J8.pin2
  N43: J10.pin2, Synerduino_AGAV_Companion_Shield_V1_1.D24
  N44: J10.pin3, Synerduino_AGAV_Companion_Shield_V1_1.D25
  N45: J12_2.pin2, J11.pin3
  N46: J12_2.pin3, J11.pin2
  N47: J6_2.pin3, Synerduino_AGAV_Companion_Shield_V1_1.A15
  N48: J6_2.pin4, Synerduino_AGAV_Companion_Shield_V1_1.A14
  N49: J6_2.pin5, Synerduino_AGAV_Companion_Shield_V1_1.A13
  N50: J6_2.pin6, Synerduino_AGAV_Companion_Shield_V1_1.A12
  N51: J6_2.pin7, Synerduino_AGAV_Companion_Shield_V1_1.A11
  N52: J6_2.pin8, Synerduino_AGAV_Companion_Shield_V1_1.A10
  N53: J6_2.pin9, Synerduino_AGAV_Companion_Shield_V1_1.A9
  N54: J6_2.pin10, Synerduino_AGAV_Companion_Shield_V1_1.A8
  N55: switch2.0, J20.pin1
  N56: switch2.1, J19.pin1
  N57: switch2.2, J19.pin10
  N58: switch2.3, J19.pin6
  N59: switch2.4, J19.pin2
  N60: switch2.5, J19.pin11
  N61: switch2.6, J19.pin7
  N62: switch2.7, J19.pin3
  N63: switch2.8, J19.pin12
  N64: switch2.9, J19.pin8
  N65: switch2.10, J19.pin4
  N66: switch2.11, J19.pin9
  N67: switch2.12, J19.pin5

notes:
  www.synerflight.com
  ~ + -
  Telemetey
  - + ~
  4B
  2B
  1C
  3A
  4A
  2A
  1B
  2C
  3B
  4C
  3C
  1A
