# Fritzing sketch synerduino pix3-analog2 (saved by Fritzing 0.9.3b)
circuit board: 13.6cm x 6.2cm
circuit board: 5.78556cm x 20cm
circuit board: 4.10404cm x 3.33229cm
circuit board: 5.78556cm x 20cm
breadboards: 1

parts:
  J17 = male pin header, 10 pins [form="♂ (male)"]  # not connected
  J18 = double row male pin header, 36 pins [form="♂ (male)"]  # not connected
  J12 = male pin header, 8 pins [form="♂ (male)"]  # not connected
  J13 = male pin header, 8 pins [form="♂ (male)"]  # not connected
  J15 = male pin header, 8 pins [form="♂ (male)"]  # not connected
  J16 = male pin header, 8 pins [form="♂ (male)"]  # not connected
  J14 = male pin header, 8 pins [form="♂ (male)"]  # not connected
  J1 = male pin header, 16 pins [form="♂ (male)"]
  CH8 = male pin header, 3 pins [form="♂ (male)"]
  CH7 = male pin header, 3 pins [form="♂ (male)"]
  CH6 = male pin header, 3 pins [form="♂ (male)"]
  CH5 = male pin header, 3 pins [form="♂ (male)"]
  CH5_2 = male pin header, 3 pins [form="♂ (male)"]
  CH3 = male pin header, 3 pins [form="♂ (male)"]
  CH2 = male pin header, 3 pins [form="♂ (male)"]
  CH1 = male pin header, 3 pins [form="♂ (male)"]
  A7 = Pad [width=2 height=1.5 connect=center]
  A6 = Pad [width=2 height=1.5 connect=center]
  A5 = Pad [width=2 height=1.5 connect=center]
  A4 = Pad [width=2 height=1.5 connect=center]
  A3 = Pad [width=2 height=1.5 connect=center]
  A2 = Pad [width=2 height=1.5 connect=center]
  A1 = Pad [width=2 height=1.5 connect=center]
  A0 = Pad [width=2 height=1.5 connect=center]
  P8 = Pad [width=2 height=1.5 connect=center]
  P7 = Pad [width=2 height=1.5 connect=center]
  P6 = Pad [width=2 height=1.5 connect=center]
  P5 = Pad [width=2 height=1.5 connect=center]
  P4 = Pad [width=2 height=1.5 connect=center]
  P3 = Pad [width=2 height=1.5 connect=center]
  P2 = Pad [width=2 height=1.5 connect=center]
  P1 = Pad [width=2 height=1.5 connect=center]
  D9 = Pad [width=2 height=1.5 connect=center]
  D8 = Pad [width=2 height=1.5 connect=center]
  D7 = Pad [width=2 height=1.5 connect=center]
  D6 = Pad [width=2 height=1.5 connect=center]
  D5 = Pad [width=2 height=1.5 connect=center]
  D4 = Pad [width=2 height=1.5 connect=center]
  D3 = Pad [width=2 height=1.5 connect=center]
  D2 = Pad [width=2 height=1.5 connect=center]
  J2 = male pin header, 16 pins [form="♂ (male)"]
  J3 = male pin header, 16 pins [form="♂ (male)"]
  J4 = female pin header, 8 pins [form="♀ (female)"]
  PPM = female pin header, 3 pins [form="♀ (female)"]
  Sbus = female pin header, 3 pins [form="♀ (female)"]
  J5 = male pin header, 10 pins [form="♂ (male)"]
  J6 = male pin header, 8 pins [form="♂ (male)"]
  J7 = female pin header, 4 pins [form="♀ (female)"]
  J9 = female pin header, 4 pins [form="♀ (female)"]
  J10 = female pin header, 4 pins [form="♀ (female)"]
  J12_2 = female pin header, 4 pins [form="♀ (female)"]
  J6_2 = male pin header, 10 pins [form="♂ (male)"]
  J8 = male pin header, 4 pins [form="♂ (male)"]
  J11 = male pin header, 4 pins [form="♂ (male)"]
  ACH1 = male pin header, 3 pins [form="♂ (male)"]
  ACH2 = male pin header, 3 pins [form="♂ (male)"]
  ACH3 = male pin header, 3 pins [form="♂ (male)"]
  ACH4 = male pin header, 3 pins [form="♂ (male)"]
  BCH1 = male pin header, 3 pins [form="♂ (male)"]
  BCH2 = male pin header, 3 pins [form="♂ (male)"]
  BCH3 = male pin header, 3 pins [form="♂ (male)"]
  CCH1 = male pin header, 3 pins [form="♂ (male)"]
  CCH2 = male pin header, 3 pins [form="♂ (male)"]
  Synerduino_AGAV_Analog_Shield_V0_1 = Arduino Mega ADK (Rev3)
  switch2 = Rotary_Switch_12x1
  J19 = male pin header, 12 pins [form="♂ (male)"]
  CCH3 = male pin header, 3 pins [form="♂ (male)"]
  CCH4 = male pin header, 3 pins [form="♂ (male)"]
  J21 = male pin header, 12 pins [form="♂ (male)"]
  J22 = female pin header, 4 pins [form="♀ (female)"]
  BCH4 = male pin header, 3 pins [form="♂ (male)"]
  IC3T = IC, DIP package, 14 pins [chip_label=IC]
  IC1T = IC, DIP package, 14 pins [chip_label=IC]
  B1 = male pin header, 4 pins [form="♂ (male)"]
  B2 = male pin header, 4 pins [form="♂ (male)"]
  B3 = male pin header, 4 pins [form="♂ (male)"]
  B4 = male pin header, 4 pins [form="♂ (male)"]
  T1 = male pin header, 4 pins [form="♂ (male)"]
  T3 = male pin header, 4 pins [form="♂ (male)"]
  G3 = male pin header, 4 pins [form="♂ (male)"]
  G2 = male pin header, 4 pins [form="♂ (male)"]
  G1 = male pin header, 4 pins [form="♂ (male)"]
  G4 = male pin header, 4 pins [form="♂ (male)"]
  R2 = Resistor [tolerance=±5% resistance=1k package=THT]
  R1 = Resistor [tolerance=±5% resistance=1k package=THT]
  R3 = Resistor [tolerance=±5% resistance=1k package=THT]
  J23 = female pin header, 2 pins [form="♀ (female)"]
  J24 = female pin header, 2 pins [form="♀ (female)"]
  J25 = female pin header, 2 pins [form="♀ (female)"]
  J20 = male pin header, 4 pins [form="♂ (male)"]

nets:
  N1: J1.pin1, PPM.pin3
  N2: J1.pin2, Sbus.pin1
  N3: J1.pin7, J22.pin1
  N4: J1.pin8, J22.pin2
  N5: J1.pin9, J22.pin3
  N6: J1.pin10, J22.pin4
  N7: J1.pin13, J6_2.pin7, Synerduino_AGAV_Analog_Shield_V0_1.A11
  N8: J1.pin14, J6_2.pin8, Synerduino_AGAV_Analog_Shield_V0_1.A10
  N9: J1.pin15, J6_2.pin9, Synerduino_AGAV_Analog_Shield_V0_1.A9
  N10: J1.pin16, J6_2.pin10, Synerduino_AGAV_Analog_Shield_V0_1.A8
  N11: CH8.pin1, P8.pad
  N12: CH8.pin2, CH7.pin2, CH6.pin2, CH5.pin2, CH5_2.pin2, CH3.pin2, CH2.pin2, CH1.pin2, J2.pin1, J2.pin2, J2.pin3, J2.pin4, J2.pin5, J2.pin6, J2.pin7, J2.pin8, J2.pin9, J2.pin10, J2.pin11, J2.pin12, J2.pin13, J2.pin14, J2.pin15, J2.pin16, PPM.pin2, J5.pin9, J6.pin7, Synerduino_AGAV_Analog_Shield_V0_1.VIN
  N13: CH8.pin3, CH7.pin3, CH6.pin3, CH5.pin3, CH5_2.pin3, CH3.pin3, CH2.pin3, CH1.pin3, J3.pin1, J3.pin2, J3.pin3, J3.pin4, J3.pin5, J3.pin6, J3.pin7, J3.pin8, J3.pin9, J3.pin10, J3.pin11, J3.pin12, J3.pin13, J3.pin14, J3.pin15, J3.pin16, PPM.pin1, Sbus.pin3, J5.pin10, J6.pin8, J12_2.pin1, J6_2.pin1, J11.pin4, ACH1.pin3, ACH2.pin3, ACH3.pin3, Synerduino_AGAV_Analog_Shield_V0_1.GND, IC3T.pin7, IC1T.pin7, B1.pin3, B2.pin3, B3.pin3, B4.pin3, R2.Pin_1, R1.Pin_1, R3.Pin_1
  N14: CH7.pin1, P7.pad
  N15: CH6.pin1, P6.pad
  N16: CH5.pin1, P5.pad
  N17: CH5_2.pin1, P4.pad
  N18: CH3.pin1, P3.pad
  N19: CH2.pin1, P2.pad
  N20: CH1.pin1, P1.pad
  N21: A7.pad, Synerduino_AGAV_Analog_Shield_V0_1.A7
  N22: A6.pad, Synerduino_AGAV_Analog_Shield_V0_1.A6
  N23: A5.pad, Synerduino_AGAV_Analog_Shield_V0_1.A5
  N24: A4.pad, Synerduino_AGAV_Analog_Shield_V0_1.A4
  N25: A3.pad, Synerduino_AGAV_Analog_Shield_V0_1.A3
  N26: A2.pad, Synerduino_AGAV_Analog_Shield_V0_1.A2
  N27: A1.pad, Synerduino_AGAV_Analog_Shield_V0_1.A1
  N28: A0.pad, Synerduino_AGAV_Analog_Shield_V0_1.A0
  N29: D9.pad, J4.pin8, J5.pin1, J6.pin2, Synerduino_AGAV_Analog_Shield_V0_1.D9_PWM
  N30: D8.pad, J4.pin7, J5.pin2, J6.pin1, Synerduino_AGAV_Analog_Shield_V0_1.D8_PWM
  N31: D7.pad, J4.pin6, J5.pin3, Synerduino_AGAV_Analog_Shield_V0_1.D7_PWM
  N32: D6.pad, J4.pin5, J5.pin4, Synerduino_AGAV_Analog_Shield_V0_1.D6_PWM
  N33: D5.pad, J4.pin4, J5.pin5, Synerduino_AGAV_Analog_Shield_V0_1.D5_PWM
  N34: D4.pad, J4.pin3, J5.pin6, Synerduino_AGAV_Analog_Shield_V0_1.D4_PWM
  N35: D3.pad, J4.pin2, J5.pin7, Synerduino_AGAV_Analog_Shield_V0_1.D3_PWM
  N36: D2.pad, J4.pin1, J5.pin8, Synerduino_AGAV_Analog_Shield_V0_1.D2_PWM
  N37: J6.pin3, Synerduino_AGAV_Analog_Shield_V0_1.D10_PWM
  N38: J6.pin4, Synerduino_AGAV_Analog_Shield_V0_1.D11_PWM
  N39: J6.pin5, Synerduino_AGAV_Analog_Shield_V0_1.D12_PWM, IC1T.pin14
  N40: J6.pin6, Synerduino_AGAV_Analog_Shield_V0_1.D13_PWM, IC3T.pin14
  N41: J7.pin1, J9.pin1, J10.pin1, J8.pin4
  N42: J7.pin2, Synerduino_AGAV_Analog_Shield_V0_1.D22
  N43: J7.pin3, Synerduino_AGAV_Analog_Shield_V0_1.D23
  N44: J7.pin4, J10.pin4, J6_2.pin2, J8.pin1, J11.pin1, ACH1.pin2, ACH2.pin2, ACH3.pin2, ACH4.pin2, BCH1.pin2, BCH2.pin2, BCH3.pin2, CCH1.pin2, CCH2.pin2, Synerduino_AGAV_Analog_Shield_V0_1.IOREF, Synerduino_AGAV_Analog_Shield_V0_1.5V, CCH3.pin2, CCH4.pin2, BCH4.pin2, B1.pin4, B2.pin4, B3.pin4, B4.pin4, T1.pin4, T3.pin4, G3.pin4, G2.pin4, G1.pin4, G4.pin4, J23.pin1, J24.pin1, J25.pin1
  N45: J9.pin2, J8.pin3
  N46: J9.pin3, J8.pin2
  N47: J10.pin2, Synerduino_AGAV_Analog_Shield_V0_1.D24
  N48: J10.pin3, Synerduino_AGAV_Analog_Shield_V0_1.D25
  N49: J12_2.pin2, J11.pin3
  N50: J12_2.pin3, J11.pin2
  N51: J6_2.pin3, Synerduino_AGAV_Analog_Shield_V0_1.A15, R3.Pin_0, J25.pin2
  N52: J6_2.pin4, Synerduino_AGAV_Analog_Shield_V0_1.A14, R2.Pin_0, J24.pin2
  N53: J6_2.pin5, Synerduino_AGAV_Analog_Shield_V0_1.A13, R1.Pin_0, J23.pin2
  N54: J6_2.pin6, Synerduino_AGAV_Analog_Shield_V0_1.A12
  N55: ACH1.pin1, J21.pin12
  N56: ACH2.pin1, J21.pin11
  N57: ACH3.pin1, J21.pin10
  N58: ACH4.pin1, J21.pin9
  N59: ACH4.pin3, BCH1.pin3
  N60: BCH1.pin1, J21.pin8
  N61: BCH2.pin1, J21.pin7
  N62: BCH2.pin3, BCH3.pin3, CCH1.pin3, CCH2.pin3, CCH3.pin3, CCH4.pin3, BCH4.pin3
  N63: BCH3.pin1, J21.pin6
  N64: CCH1.pin1, J21.pin4
  N65: CCH2.pin1, J21.pin3
  N66: Synerduino_AGAV_Analog_Shield_V0_1.D19/RX1, IC1T.pin5, IC1T.pin9, T1.pin2
  N67: Synerduino_AGAV_Analog_Shield_V0_1.D18/TX1, IC1T.pin3, IC1T.pin11, T1.pin1
  N68: Synerduino_AGAV_Analog_Shield_V0_1.D15/RX3, IC3T.pin5, IC3T.pin9, T3.pin2
  N69: Synerduino_AGAV_Analog_Shield_V0_1.D14/TX3, IC3T.pin3, IC3T.pin11, T3.pin1
  N70: Synerduino_AGAV_Analog_Shield_V0_1.D26, IC3T.pin1, IC3T.pin4
  N71: Synerduino_AGAV_Analog_Shield_V0_1.D27, IC3T.pin10, IC3T.pin13
  N72: Synerduino_AGAV_Analog_Shield_V0_1.D28, IC1T.pin1, IC1T.pin4
  N73: Synerduino_AGAV_Analog_Shield_V0_1.D29, IC1T.pin10, IC1T.pin13
  N74: switch2.0, J20.pin1
  N75: switch2.1, J19.pin1
  N76: switch2.2, J19.pin10
  N77: switch2.3, J19.pin6
  N78: switch2.4, J19.pin2
  N79: switch2.5, J19.pin11
  N80: switch2.6, J19.pin7
  N81: switch2.7, J19.pin3
  N82: switch2.8, J19.pin12
  N83: switch2.9, J19.pin8
  N84: switch2.10, J19.pin4
  N85: switch2.11, J19.pin9
  N86: switch2.12, J19.pin5
  N87: CCH3.pin1, J21.pin2
  N88: CCH4.pin1, J21.pin1
  N89: J21.pin5, BCH4.pin1
  N90: IC3T.pin2, B4.pin1
  N91: IC3T.pin6, B4.pin2
  N92: IC3T.pin8, B3.pin2
  N93: IC3T.pin12, B3.pin1
  N94: IC1T.pin2, B2.pin1
  N95: IC1T.pin6, B2.pin2
  N96: IC1T.pin8, B1.pin2
  N97: IC1T.pin12, B1.pin1
  N98: T1.pin3, T3.pin3
  N99: G3.pin1, G2.pin1, G1.pin1, G4.pin1
  N100: G3.pin2, G2.pin2, G1.pin2, G4.pin2
  N101: G3.pin3, G2.pin3, G1.pin3, G4.pin3

notes:
  www.synerflight.com
  ~ + -
  Telemetey
  - + ~
  4B
  2B
  1C
  3A
  4A
  2A
  1B
  2C
  3B
  4C
  3C
  1A
  + - Rx Tx
  - 22 21 +
  - 24 23 +
  T1 28 29
  T3 26 27
  29 28
  27 26
  <D13 ARM D12>
  74LS08N
  A8 A9 A10 A11
  M1 M2 M3 M4
