# Fritzing sketch synerduino pix4-2 (saved by Fritzing 0.9.3b)
circuit board: 13.6cm x 6.2cm
circuit board: 5.78556cm x 20cm
circuit board: 5.78556cm x 20cm
breadboards: 1

parts:
  Synerduino_AGAV_Shield_V0_1 = Arduino Mega ADK (Rev3)
  J18 = male pin header, 10 pins [form="♂ (male)"]  # not connected
  J21 = double row male pin header, 36 pins [form="♂ (male)"]  # not connected
  J22 = male pin header, 8 pins [form="♂ (male)"]  # not connected
  J23 = male pin header, 8 pins [form="♂ (male)"]  # not connected
  J20 = male pin header, 8 pins [form="♂ (male)"]  # not connected
  J19 = male pin header, 8 pins [form="♂ (male)"]  # not connected
  J24 = male pin header, 8 pins [form="♂ (male)"]  # not connected
  J1 = male pin header, 16 pins [form="♂ (male)"]
  CH8 = male pin header, 3 pins [form="♂ (male)"]
  CH7 = male pin header, 3 pins [form="♂ (male)"]
  CH6 = male pin header, 3 pins [form="♂ (male)"]
  CH5 = male pin header, 3 pins [form="♂ (male)"]
  CH5_2 = male pin header, 3 pins [form="♂ (male)"]
  CH3 = male pin header, 3 pins [form="♂ (male)"]
  CH2 = male pin header, 3 pins [form="♂ (male)"]
  CH1 = male pin header, 3 pins [form="♂ (male)"]
  A7 = Pad [width=2 height=1.5 connect=center]
  A6 = Pad [width=2 height=1.5 connect=center]
  A5 = Pad [width=2 height=1.5 connect=center]
  A4 = Pad [width=2 height=1.5 connect=center]
  A3 = Pad [width=2 height=1.5 connect=center]
  A2 = Pad [width=2 height=1.5 connect=center]
  A1 = Pad [width=2 height=1.5 connect=center]
  A0 = Pad [width=2 height=1.5 connect=center]
  P8 = Pad [width=2 height=1.5 connect=center]
  P7 = Pad [width=2 height=1.5 connect=center]
  P6 = Pad [width=2 height=1.5 connect=center]
  P5 = Pad [width=2 height=1.5 connect=center]
  P4 = Pad [width=2 height=1.5 connect=center]
  P3 = Pad [width=2 height=1.5 connect=center]
  P2 = Pad [width=2 height=1.5 connect=center]
  P1 = Pad [width=2 height=1.5 connect=center]
  D9 = Pad [width=2 height=1.5 connect=center]
  D8 = Pad [width=2 height=1.5 connect=center]
  D7 = Pad [width=2 height=1.5 connect=center]
  D6 = Pad [width=2 height=1.5 connect=center]
  D5 = Pad [width=2 height=1.5 connect=center]
  D4 = Pad [width=2 height=1.5 connect=center]
  D3 = Pad [width=2 height=1.5 connect=center]
  D2 = Pad [width=2 height=1.5 connect=center]
  J2 = male pin header, 16 pins [form="♂ (male)"]
  J3 = male pin header, 16 pins [form="♂ (male)"]
  J4 = female pin header, 8 pins [form="♀ (female)"]
  PPM = female pin header, 3 pins [form="♀ (female)"]
  Sbus = female pin header, 3 pins [form="♀ (female)"]
  J5 = male pin header, 10 pins [form="♂ (male)"]
  J14 = male pin header, 8 pins [form="♂ (male)"]
  J6 = male pin header, 10 pins [form="♂ (male)"]
  J11 = male pin header, 4 pins [form="♂ (male)"]
  U5 = Optocoupler [package=THT]
  U1 = Optocoupler [package=THT]
  U6 = Optocoupler [package=THT]
  U2 = Optocoupler [package=THT]
  U7 = Optocoupler [package=THT]
  U3 = Optocoupler [package=THT]
  U4 = Optocoupler [package=THT]
  U8 = Optocoupler [package=THT]
  R1 = Resistor [tolerance=±5% resistance=200 package=THT]
  R2 = Resistor [tolerance=±5% resistance=200 package=THT]
  R3 = Resistor [tolerance=±5% resistance=200 package=THT]
  R4 = Resistor [tolerance=±5% resistance=200 package=THT]
  R5 = Resistor [tolerance=±5% resistance=200 package=THT]
  R6 = Resistor [tolerance=±5% resistance=200 package=THT]
  R7 = Resistor [tolerance=±5% resistance=200 package=THT]
  R8 = Resistor [tolerance=±5% resistance=200 package=THT]
  R9 = Resistor [tolerance=±5% resistance=2k package=THT]
  R10 = Resistor [tolerance=±5% resistance=2k package=THT]
  R11 = Resistor [tolerance=±5% resistance=2k package=THT]
  R12 = Resistor [tolerance=±5% resistance=2k package=THT]
  R13 = Resistor [tolerance=±5% resistance=2k package=THT]
  R14 = Resistor [tolerance=±5% resistance=2k package=THT]
  R15 = Resistor [tolerance=±5% resistance=2k package=THT]
  R16 = Resistor [tolerance=±5% resistance=2k package=THT]
  R17 = Resistor [tolerance=±5% resistance=1k package=THT]
  R18 = Resistor [tolerance=±5% resistance=1k package=THT]
  R19 = Resistor [tolerance=±5% resistance=1k package=THT]
  R20 = Resistor [tolerance=±5% resistance=1k package=THT]
  R21 = Resistor [tolerance=±5% resistance=1k package=THT]
  R22 = Resistor [tolerance=±5% resistance=1k package=THT]
  R23 = Resistor [tolerance=±5% resistance=1k package=THT]
  R24 = Resistor [tolerance=±5% resistance=1k package=THT]
  J17 = double row female pin header, 16 pins [form="♀ (female)"]
  D10 = Pad [width=2 height=1.5 connect=center]
  D11 = Pad [width=2 height=1.5 connect=center]
  D12 = Pad [width=2 height=1.5 connect=center]
  D13 = Pad [width=2 height=1.5 connect=center]
  J13 = male pin header, 4 pins [form="♂ (male)"]
  IC2 = IC, DIP package, 14 pins [chip_label=IC]
  J25 = male pin header, 4 pins [form="♂ (male)"]
  IC1 = IC, DIP package, 14 pins [chip_label=IC]
  J26 = male pin header, 4 pins [form="♂ (male)"]
  J27 = male pin header, 12 pins [form="♂ (male)"]

nets:
  N1: Synerduino_AGAV_Shield_V0_1.A8, J1.pin16, J6.pin10
  N2: Synerduino_AGAV_Shield_V0_1.A9, J1.pin15, J6.pin9
  N3: Synerduino_AGAV_Shield_V0_1.A10, J1.pin14, J6.pin8
  N4: Synerduino_AGAV_Shield_V0_1.A11, J1.pin13, J6.pin7
  N5: Synerduino_AGAV_Shield_V0_1.A12, J6.pin6
  N6: Synerduino_AGAV_Shield_V0_1.A13, J6.pin5
  N7: Synerduino_AGAV_Shield_V0_1.A14, J6.pin4
  N8: Synerduino_AGAV_Shield_V0_1.A15, J6.pin3
  N9: Synerduino_AGAV_Shield_V0_1.A0, A0.pad
  N10: Synerduino_AGAV_Shield_V0_1.A1, A1.pad
  N11: Synerduino_AGAV_Shield_V0_1.A2, A2.pad
  N12: Synerduino_AGAV_Shield_V0_1.A3, A3.pad
  N13: Synerduino_AGAV_Shield_V0_1.A4, A4.pad
  N14: Synerduino_AGAV_Shield_V0_1.A5, A5.pad
  N15: Synerduino_AGAV_Shield_V0_1.A6, A6.pad
  N16: Synerduino_AGAV_Shield_V0_1.A7, A7.pad
  N17: Synerduino_AGAV_Shield_V0_1.D21/SCL, J27.pin1
  N18: Synerduino_AGAV_Shield_V0_1.D20/SDA, J27.pin2
  N19: Synerduino_AGAV_Shield_V0_1.D19/RX1, J27.pin3
  N20: Synerduino_AGAV_Shield_V0_1.D18/TX1, J27.pin4
  N21: Synerduino_AGAV_Shield_V0_1.D17/RX2, J27.pin5
  N22: Synerduino_AGAV_Shield_V0_1.D16/TX2, J27.pin6
  N23: Synerduino_AGAV_Shield_V0_1.D15/RX3, J27.pin7
  N24: Synerduino_AGAV_Shield_V0_1.D14/TX3, J27.pin8
  N25: Synerduino_AGAV_Shield_V0_1.GND, CH8.pin3, CH7.pin3, CH6.pin3, CH5.pin3, CH5_2.pin3, CH3.pin3, CH2.pin3, CH1.pin3, J3.pin1, J3.pin2, J3.pin3, J3.pin4, J3.pin5, J3.pin6, J3.pin7, J3.pin8, J3.pin9, J3.pin10, J3.pin11, J3.pin12, J3.pin13, J3.pin14, J3.pin15, J3.pin16, PPM.pin1, Sbus.pin3, J5.pin10, J14.pin8, J6.pin1, U5.Pin_2, U1.Pin_2, U6.Pin_2, U2.Pin_2, U7.Pin_2, U3.Pin_2, U4.Pin_2, U8.Pin_2, R9.Pin_0, R10.Pin_0, R11.Pin_0, R12.Pin_0, R13.Pin_0, R14.Pin_0, R15.Pin_0, R16.Pin_0, IC2.pin7, J25.pin3, IC1.pin7, J26.pin3, J27.pin12
  N26: Synerduino_AGAV_Shield_V0_1.D13_PWM, J14.pin6
  N27: Synerduino_AGAV_Shield_V0_1.D12_PWM, J14.pin5
  N28: Synerduino_AGAV_Shield_V0_1.D11_PWM, J14.pin4
  N29: Synerduino_AGAV_Shield_V0_1.D10_PWM, J14.pin3
  N30: Synerduino_AGAV_Shield_V0_1.D9_PWM, D9.pad, J4.pin8, J5.pin1, J14.pin2
  N31: Synerduino_AGAV_Shield_V0_1.D8_PWM, D8.pad, J4.pin7, J5.pin2, J14.pin1
  N32: Synerduino_AGAV_Shield_V0_1.IOREF, Synerduino_AGAV_Shield_V0_1.5V, J6.pin2, J25.pin4, J26.pin4, J27.pin11
  N33: Synerduino_AGAV_Shield_V0_1.VIN, CH8.pin2, CH7.pin2, CH6.pin2, CH5.pin2, CH5_2.pin2, CH3.pin2, CH2.pin2, CH1.pin2, J2.pin1, J2.pin3, J2.pin4, J2.pin5, J2.pin6, J2.pin7, J2.pin8, J2.pin9, J2.pin10, J2.pin11, J2.pin12, J2.pin13, J2.pin14, J2.pin15, J2.pin16, PPM.pin2, J5.pin9, J14.pin7, J17.pin1, J17.pin2, J17.pin3, J17.pin4, J17.pin5, J17.pin6, J17.pin7, J17.pin8
  N34: Synerduino_AGAV_Shield_V0_1.D0/RX0, J27.pin9
  N35: Synerduino_AGAV_Shield_V0_1.D1/TX0, J27.pin10
  N36: Synerduino_AGAV_Shield_V0_1.D2_PWM, D2.pad, J4.pin1, J5.pin8
  N37: Synerduino_AGAV_Shield_V0_1.D3_PWM, D3.pad, J4.pin2, J5.pin7
  N38: Synerduino_AGAV_Shield_V0_1.D4_PWM, D4.pad, J4.pin3, J5.pin6
  N39: Synerduino_AGAV_Shield_V0_1.D5_PWM, D5.pad, J4.pin4, J5.pin5
  N40: Synerduino_AGAV_Shield_V0_1.D6_PWM, D6.pad, J4.pin5, J5.pin4
  N41: Synerduino_AGAV_Shield_V0_1.D7_PWM, D7.pad, J4.pin6, J5.pin3
  N42: Synerduino_AGAV_Shield_V0_1.D22, IC2.pin14
  N43: Synerduino_AGAV_Shield_V0_1.D23, IC1.pin14
  N44: Synerduino_AGAV_Shield_V0_1.D26, R17.Pin_0, R20.Pin_0
  N45: Synerduino_AGAV_Shield_V0_1.D27, R21.Pin_0, R23.Pin_0
  N46: Synerduino_AGAV_Shield_V0_1.D28, R18.Pin_0, R19.Pin_0
  N47: Synerduino_AGAV_Shield_V0_1.D29, R22.Pin_0, R24.Pin_0
  N48: Synerduino_AGAV_Shield_V0_1.D42, IC2.pin1, IC2.pin4
  N49: Synerduino_AGAV_Shield_V0_1.D43, IC2.pin10, IC2.pin13
  N50: Synerduino_AGAV_Shield_V0_1.D44, IC1.pin1, IC1.pin4
  N51: Synerduino_AGAV_Shield_V0_1.D45, IC1.pin10, IC1.pin13
  N52: J1.pin1, D11.pad
  N53: J1.pin2, D13.pad
  N54: J1.pin3, R7.Pin_1
  N55: J1.pin4, R6.Pin_1
  N56: J1.pin5, R3.Pin_1
  N57: J1.pin6, R2.Pin_1
  N58: J1.pin7, J1.pin8, J1.pin9, J1.pin10, R1.Pin_1, R4.Pin_1, R5.Pin_1, R8.Pin_1
  N59: CH8.pin1, P8.pad
  N60: CH7.pin1, P7.pad
  N61: CH6.pin1, P6.pad
  N62: CH5.pin1, P5.pad
  N63: CH5_2.pin1, P4.pad
  N64: CH3.pin1, P3.pad
  N65: CH2.pin1, P2.pad
  N66: CH1.pin1, P1.pad
  N67: J2.pin2, Sbus.pin2
  N68: PPM.pin3, D10.pad
  N69: Sbus.pin1, D12.pad
  N70: J11.pin1, IC2.pin2
  N71: J11.pin2, IC2.pin6
  N72: J11.pin3, IC2.pin12
  N73: J11.pin4, IC2.pin8
  N74: U5.Pin_1, R2.Pin_0
  N75: U5.Pin_4, R9.Pin_1, J17.pin13
  N76: U5.Pin_5, R23.Pin_1
  N77: U1.Pin_1, R1.Pin_0
  N78: U1.Pin_4, R10.Pin_1, J17.pin9
  N79: U1.Pin_5, R24.Pin_1
  N80: U6.Pin_1, R3.Pin_0
  N81: U6.Pin_4, R11.Pin_1, J17.pin14
  N82: U6.Pin_5, R21.Pin_1
  N83: U2.Pin_1, R4.Pin_0
  N84: U2.Pin_4, R12.Pin_1, J17.pin10
  N85: U2.Pin_5, R22.Pin_1
  N86: U7.Pin_1, R6.Pin_0
  N87: U7.Pin_4, R14.Pin_1, J17.pin15
  N88: U7.Pin_5, R20.Pin_1
  N89: U3.Pin_1, R5.Pin_0
  N90: U3.Pin_4, R13.Pin_1, J17.pin11
  N91: U3.Pin_5, R19.Pin_1
  N92: U4.Pin_1, R8.Pin_0
  N93: U4.Pin_4, R16.Pin_1, J17.pin12
  N94: U4.Pin_5, R18.Pin_1
  N95: U8.Pin_1, R7.Pin_0
  N96: U8.Pin_4, R15.Pin_1, J17.pin16
  N97: U8.Pin_5, R17.Pin_1
  N98: J13.pin1, IC1.pin2
  N99: J13.pin2, IC1.pin6
  N100: J13.pin3, IC1.pin12
  N101: J13.pin4, IC1.pin8
  N102: IC2.pin3, IC2.pin11, J25.pin2, IC1.pin3, IC1.pin11, J26.pin2
  N103: IC2.pin5, IC2.pin9, J25.pin1, IC1.pin5, IC1.pin9, J26.pin1

notes:
  www.synerflight.com
  ~ + -
  Telemetey
  - + ~
  1 2 3 4 5 6 7 8
  P S 8 7 6 5 4 3 2 1
  RC PWM IN
  pwm converter
  Motor PWM in
  RC in
  Motor PWM Out
  ~
  2K
  200Ω
  - 22 21 +
  >M26
  >M27
  >M28
  >M29
  1K
  - 24 23 +
  Rx3 Tx3 Rx3 Tx3
  Rx1 Tx1 Rx3 Tx3
  + - Tx Rx
  Rx1 Tx1 Rx1 Tx1
  <45-44 43-42>
  <45 44-43 42>
  <D23 ARM D22>
  74LS08N
  4 3 2 1
  A8
  A9
  A10
  A11
