# Fritzing sketch synerduino STM micro (saved by Fritzing 0.9.3b)
circuit board: 10.5cm x 6.2cm
circuit board: 8cm x 2.6cm
breadboards: 1

parts:
  Synerduino_Micro_Stick_Shield = Arduino Nano (Rev3.0)
  IMU = InvenSense MPU6050
  J1 = Screw terminal - 2 pins [package=THT]
  D3 = male pin header, 3 pins [form="♂ (male)"]
  D9 = male pin header, 3 pins [form="♂ (male)"]
  D10 = male pin header, 3 pins [form="♂ (male)"]
  D11 = male pin header, 3 pins [form="♂ (male)"]
  S1 = female pin header, 4 pins [form="♀ (female)"]
  D2 = male pin header, 3 pins [form="♂ (male)"]
  G = Pad [width=1.2 height=3 connect=center]  # not connected
  3 = Pad [width=1.2 height=3 connect=center]  # not connected
  C = Pad [width=1.2 height=3 connect=center]  # not connected
  D = Pad [width=1.2 height=3 connect=center]  # not connected
  XD = Pad [width=1.2 height=3 connect=center]  # not connected
  XC = Pad [width=1.2 height=3 connect=center]  # not connected
  A = Pad [width=1.2 height=3 connect=center]  # not connected
  IN = Pad [width=1.2 height=3 connect=center]  # not connected
  J2 = rounded female pin header, 15 pins [form="♀ (female rounded)"]  # not connected
  J3 = female pin header, 15 pins [form="♀ (female)"]  # not connected
  J15 = rounded female pin header, 20 pins [form="♀ (female rounded)"]
  J16 = rounded female pin header, 20 pins [form="♀ (female rounded)"]
  IMU2 = InvenSense MPU6050
  J17 = male pin header, 4 pins [form="♂ (male)"]  # not connected
  J20 = female pin header, 8 pins [form="♀ (female)"]
  Synerduino_STM_UNO = Arduino Uno (Rev3)
  N3 = male pin header, 3 pins [form="♂ (male)"]
  N4 = male pin header, 3 pins [form="♂ (male)"]
  N5 = male pin header, 3 pins [form="♂ (male)"]
  N6 = male pin header, 3 pins [form="♂ (male)"]
  N7 = male pin header, 3 pins [form="♂ (male)"]
  N8 = male pin header, 3 pins [form="♂ (male)"]
  U1 = Voltage Regulator - 5V [package="TO220 [THT]"]
  S7 = male pin header, 3 pins [form="♂ (male)"]
  U2 = Voltage Regulator - 5V [package="TO220 [THT]"]
  D12 = Rectifier Diode [part_number=1N4001 package="300 mil [THT]"]
  C2 = Electrolytic Capacitor [capacitance=470µF voltage=35V part_number=470µF package="200 mil [THT, electrolytic]"]
  -_+1 = screw terminal, 2 pins
  0_-_+1 = screw terminal, 2 pins
  -_+_3 = screw terminal, 2 pins
  -_+_2 = screw terminal, 2 pins
  4_-_+ = screw terminal, 2 pins
  N2 = male pin header, 3 pins [form="♂ (male)"]
  N1 = male pin header, 3 pins [form="♂ (male)"]
  S6 = male pin header, 3 pins [form="♂ (male)"]
  S5 = male pin header, 3 pins [form="♂ (male)"]
  S4 = male pin header, 3 pins [form="♂ (male)"]
  S3 = male pin header, 3 pins [form="♂ (male)"]
  S2 = male pin header, 3 pins [form="♂ (male)"]
  S1_2 = male pin header, 3 pins [form="♂ (male)"]
  J39 = male pin header, 4 pins [form="♂ (male)"]  # not connected
  J19 = female pin header, 3 pins [form="♀ (female)"]
  J18 = female pin header, 3 pins [form="♀ (female)"]
  Sbus = Pad [width=1.5 height=1.5 connect=center]
  N0 = male pin header, 3 pins [form="♂ (male)"]
  P1 = Pad [width=1.5 height=1.5 connect=center]
  PPM = Pad [width=1.5 height=1.5 connect=center]
  J29 = male pin header, 6 pins [form="♂ (male)"]  # not connected
  J40 = male pin header, 5 pins [form="♂ (male)"]

nets:
  N1: Synerduino_Micro_Stick_Shield.D1/TX, S1.pin1
  N2: Synerduino_Micro_Stick_Shield.D0/RX, S1.pin2
  N3: Synerduino_Micro_Stick_Shield.D2, D2.pin1
  N4: Synerduino_Micro_Stick_Shield.D3, D3.pin1
  N5: Synerduino_Micro_Stick_Shield.D9, D9.pin1
  N6: Synerduino_Micro_Stick_Shield.D10, D10.pin1
  N7: Synerduino_Micro_Stick_Shield.D11/MOSI, D11.pin1
  N8: Synerduino_Micro_Stick_Shield.VIN, J1.pin1, D3.pin2, D9.pin2, D10.pin2, D11.pin2, S1.pin4, D2.pin2
  N9: Synerduino_Micro_Stick_Shield.A5, IMU.SCL
  N10: Synerduino_Micro_Stick_Shield.A4, IMU.SDA
  3V3: Synerduino_Micro_Stick_Shield.3V3, IMU.VCC
  N11: IMU.GND, J1.pin2, D3.pin3, D9.pin3, D10.pin3, D11.pin3, S1.pin3, D2.pin3
  GND: J15.pin2, U1.GND, U2.GND, C2.-, -_+1.pin2, 0_-_+1.pin2, -_+_3.pin2, -_+_2.pin2, 4_-_+.pin2
  N12: J15.pin4, S3.pin1
  N13: J15.pin7, S7.pin1
  N14: J15.pin12, N0.pin1, P1.pad
  N15: J15.pin15, S5.pin1
  N16: J16.pin5, S1_2.pin1
  N17: J16.pin10, S4.pin1
  N18: J16.pin11, S2.pin1
  N19: J16.pin12, S6.pin1
  N20: J16.pin16, IMU2.SCL
  N21: J16.pin17, IMU2.SDA
  N22: J16.pin18, U2.output_voltage
  GND_2: J16.pin19, IMU2.GND, Synerduino_STM_UNO.GND, N3.pin3, N4.pin3, N5.pin3, N6.pin3, N7.pin3, N8.pin3, S7.pin3, N2.pin3, N1.pin3, S6.pin3, S5.pin3, S4.pin3, S3.pin3, S2.pin3, S1_2.pin3, J19.pin1, J18.pin3, N0.pin3
  N23: J16.pin20, IMU2.VCC
  N24: J20.pin1, Synerduino_STM_UNO.D9_PWM, N8.pin1
  N25: J20.pin2, Synerduino_STM_UNO.D8, N7.pin1
  N26: J20.pin3, Synerduino_STM_UNO.D7, N6.pin1
  N27: J20.pin4, Synerduino_STM_UNO.D6_PWM, N5.pin1
  N28: J20.pin5, Synerduino_STM_UNO.D5_PWM, N4.pin1
  N29: J20.pin6, Synerduino_STM_UNO.D4, N3.pin1
  N30: J20.pin7, Synerduino_STM_UNO.D3_PWM, N2.pin1
  N31: J20.pin8, Synerduino_STM_UNO.D2, N1.pin1
  N32: Synerduino_STM_UNO.A0, J40.pin5
  N33: Synerduino_STM_UNO.A1, J40.pin4
  N34: Synerduino_STM_UNO.A2, J40.pin3
  N35: Synerduino_STM_UNO.A3, J40.pin2
  N36: Synerduino_STM_UNO.A4/SDA, J40.pin1
  N37: Synerduino_STM_UNO.VIN, N3.pin2, N4.pin2, N5.pin2, N6.pin2, N7.pin2, N8.pin2, U1.output_voltage, S7.pin2, N2.pin2, N1.pin2, S6.pin2, S5.pin2, S4.pin2, S3.pin2, S2.pin2, S1_2.pin2, J19.pin2, J18.pin2, N0.pin2
  N38: U1.input_voltage, U2.input_voltage, D12.cathode
  N39: D12.anode, C2.+, -_+1.pin1, 0_-_+1.pin1, -_+_3.pin1, -_+_2.pin1, 4_-_+.pin1
  N40: J19.pin3, Sbus.pad
  N41: J18.pin1, PPM.pad

notes:
  Tx Rx
  Rx Tx
  N8 N7 N6 N5 N4 N3 N2 N1
  Soft Serial
  GPS UART1 /  UART2
  PPM SBUS
